# Fritzing sketch complete (saved by Fritzing 0.9.3b)
breadboards: 1

parts:
  Part1 = Arduino Uno (Rev3)
  S1 = Momentary Switch [package=ksa_sealed_tac_switch]
  J1 = Basic Servo
  R1 = Resistor [tolerance=±5% resistance=1k package=THT]

nets:
  N1: Part1.D8, J1.pulse
  N2: Part1.D7, S1.2, R1.Pin_0
  5V: Part1.5V, S1.4, J1.vcc
  GND: Part1.GND, J1.gnd, R1.Pin_1
