# Fritzing sketch servobutton (saved by Fritzing 0.9.3b)
breadboards: 1

parts:
  Part1 = Arduino Uno (Rev3)
  S1 = Momentary Switch [package=ksa_sealed_tac_switch]

nets:
  N1: Part1.D7, S1.4
  N2: Part1.GND, S1.2
