# Fritzing sketch parallel buzzer (saved by Fritzing 0.9.3b)
breadboards: 1

parts:
  R1 = Resistor [tolerance=±5% resistance=22k package=THT]
  R2 = Resistor [tolerance=±5% resistance=22k package=THT]
  R3 = Resistor [tolerance=±5% resistance=22k package=THT]
  PSU1 = Adjustable Breadboard Power Supply  # not connected
  VCC1 = Battery block 9V  # not connected
  SG1 = Buzzer 12mm [package=buzzer-12mm-ns]

nets:
  N1: R1.Pin_0, R2.Pin_0, R3.Pin_0
  N2: R1.Pin_1, R2.Pin_1, R3.Pin_1, SG1.1
