# Fritzing sketch series buzzer (saved by Fritzing 0.9.3b)
breadboards: 1

parts:
  R3 = Resistor [tolerance=±5% resistance=100 package=THT]
  PSU1 = Adjustable Breadboard Power Supply  # not connected
  VCC1 = Battery block 9V  # not connected
  R4 = Resistor [tolerance=±5% resistance=100 package=THT]
  R5 = Resistor [tolerance=±5% resistance=100 package=THT]
  SG1 = Buzzer 12mm [package=buzzer-12mm-ns]

nets:
  N1: R3.Pin_1, R4.Pin_0
  N2: R4.Pin_1, R5.Pin_0
  N3: R5.Pin_1, SG1.1
