# Fritzing sketch arduino_LED (saved by Fritzing 0.9.3b)
breadboards: 1

parts:
  Part1 = Arduino Uno (Rev3)
  R1 = Resistor [tolerance=±5% resistance=220 package=THT]
  LED1 = LED - 5mm [color="White (6500K)" package="5 mm [THT]"]
  VCC1 = Battery block 9V  # not connected
  Part2 = Arduino Uno (Rev3)  # not connected
  USBTTL1 = USB TTL Serial Cable  # not connected
  Part3 = Arduino Uno (Rev3)  # not connected

nets:
  N1: Part1.D7, R1.Pin_0
  N2: Part1.GND, LED1.cathode
  N3: R1.Pin_1, LED1.anode
