# Fritzing sketch arduino_LED2 (saved by Fritzing 0.9.3b)
breadboards: 1

parts:
  Part1 = Arduino Uno (Rev3)
  R1 = Resistor [tolerance=±5% resistance=220 package=THT]
  LED1 = LED - 5mm [color="White (6500K)" package="5 mm [THT]"]
  VCC1 = Battery block 9V  # not connected
  LED2 = LED - 5mm [color="White (6500K)" package="5 mm [THT]"]
  R2 = Resistor [tolerance=±5% resistance=220 package=THT]

nets:
  N1: Part1.D12/MISO, R2.Pin_0
  N2: Part1.D7, R1.Pin_0
  N3: Part1.GND, LED1.cathode, LED2.cathode
  N4: R1.Pin_1, LED1.anode
  N5: LED2.anode, R2.Pin_1
