# Fritzing sketch vib and lecd (saved by Fritzing 0.9.3b)
breadboards: 1

parts:
  PSU1 = Adjustable Breadboard Power Supply  # not connected
  VCC1 = Battery block 9V  # not connected
  MOTOR1 = Vibration Motor
  R1 = Trimmer Potentiometer [maximum_resistance=10kΩ package=THT]
  R2 = Resistor [tolerance=±5% resistance=1k package=THT]
  LED1 = LED - 5mm [color="Red (633nm)" package="5 mm [THT]"]  # not connected

nets:
  N1: MOTOR1.POS, R1.leg2, R2.Pin_0

custom parts:
  Vibration Motor: An eccentric vibration motor!
