# Fritzing sketch solar project example (saved by Fritzing 0.9.3b)
breadboards: 1

parts:
  Solar_Panel1 = SOLAR-IXYS [package=solarbit-12x1]
  Diode = Rectifier Diode [part_number=1N4001 package="300 mil [THT]"]
  LED = LED - 5mm [color="White (6500K)" package="5 mm [THT]"]
  Switch = SWITCH_SPDT [package=kps-1290]
  BATT1 = 3xAAA Switchable Battery Pack w/Bare Wire
  Resistor = Resistor [tolerance=±5% resistance=100 package=THT]
  Solar_Panel2 = SOLAR-IXYS [package=solarbit-12x1]

nets:
  N1: Solar_Panel1.A, Solar_Panel2.C
  N2: Solar_Panel1.C, Diode.anode
  N3: Diode.cathode, Switch.O, BATT1.POS
  N4: LED.cathode, BATT1.NEG, Solar_Panel2.A
  N5: LED.anode, Resistor.Pin_1
  N6: Switch.P, Resistor.Pin_0

custom parts:
  3xAAA Switchable Battery Pack w/Bare Wire: 3xAAA Switchable Battery Pack w/Bare Wire Connectors
